# Fritzing sketch Schema de conexiuni (saved by Fritzing 0.9.4)
perfboards: 1

parts:
  Mega_2560 = Arduino Mega 2560 (Rev3)
  Punte_H_L298_/_Drive_Motoare = L298N DC motor driver
  Baterie_9V_/_Sursa_9V_DC = BC9VPC [package=bc9vpc]
  Motor_Dreapta = DC Motor
  Motor_Stanga = DC Motor
  HC-SR04_Sensor_1 = HC-SR04 Ultrasonic Distance Sensor
  S1 = TCRT5000 [package=THT]  # not connected
  S2 = TCRT5000 [package=THT]  # not connected
  S3 = TCRT5000 [package=THT]  # not connected
  S4 = TCRT5000 [package=THT]  # not connected
  S5 = TCRT5000 [package=THT]  # not connected
  Near = TCRT5000 [package=THT]  # not connected
  Servo_Motor_Rotire_Senzor_US = Basic Servo
  Afisare_directie_8x8_LED = 8x8 LED Modul mit MAX7219 [package=THT]
  Selectie_Mod_Functionare = Round Pushbutton
  D2F2 = D2F-FL Omron Snap Action Limit Switch with Level  # not connected
  LCD2004-I2C1 = LCD2004-I2C
  Bară_de_neopixeli_pentru_Semnalizare = WS2812 RGB LED matrix 1x8

nets:
  GND: Mega_2560.GND, Punte_H_L298_/_Drive_Motoare.GND, Baterie_9V_/_Sursa_9V_DC.V-, HC-SR04_Sensor_1.GND, Servo_Motor_Rotire_Senzor_US.gnd, Afisare_directie_8x8_LED.GND_Eingang, LCD2004-I2C1.GND, Bară_de_neopixeli_pentru_Semnalizare.GND
  N1: Mega_2560.D8_PWM, Bară_de_neopixeli_pentru_Semnalizare.DIN
  VCC: Mega_2560.5V, Punte_H_L298_/_Drive_Motoare.5V, HC-SR04_Sensor_1.VCC, Servo_Motor_Rotire_Senzor_US.vcc, Afisare_directie_8x8_LED.VCC_Eingang, Selectie_Mod_Functionare.leg1, LCD2004-I2C1.VCC, Bară_de_neopixeli_pentru_Semnalizare.VCC
  N2: Mega_2560.D2_PWM, Punte_H_L298_/_Drive_Motoare.ENA
  N3: Mega_2560.D3_PWM, Punte_H_L298_/_Drive_Motoare.ENB
  N4: Mega_2560.D4_PWM, Servo_Motor_Rotire_Senzor_US.pulse
  N5: Mega_2560.D5_PWM, HC-SR04_Sensor_1.ECHO
  N6: Mega_2560.D6_PWM, Afisare_directie_8x8_LED.CS_Eingang
  N7: Mega_2560.D7_PWM, Afisare_directie_8x8_LED.CLK_Eingang
  N8: Mega_2560.D22, Punte_H_L298_/_Drive_Motoare.IN1
  N9: Mega_2560.D23, Punte_H_L298_/_Drive_Motoare.IN2
  N10: Mega_2560.D24, Punte_H_L298_/_Drive_Motoare.IN3
  N11: Mega_2560.D25, Punte_H_L298_/_Drive_Motoare.IN4
  N12: Mega_2560.D33, Selectie_Mod_Functionare.leg0
  N13: Mega_2560.D34, HC-SR04_Sensor_1.TRIG
  N14: Mega_2560.D35, Afisare_directie_8x8_LED.DIN_Eingang
  N15: Punte_H_L298_/_Drive_Motoare.OUT1, Motor_Stanga.pin_2
  N16: Punte_H_L298_/_Drive_Motoare.OUT2, Motor_Stanga.pin_1
  N17: Punte_H_L298_/_Drive_Motoare.OUT3, Motor_Dreapta.pin_2
  N18: Punte_H_L298_/_Drive_Motoare.OUT4, Motor_Dreapta.pin_1
  N19: Punte_H_L298_/_Drive_Motoare.12V, Baterie_9V_/_Sursa_9V_DC.V+

notes:
  Near
  CLP
  S5
  S4
  S3
  S2
  S1
  GND
  VCC
  Modul IR TCRT5000
  Mega 2560 Pin 20 SDA
  Mega 2560 Pin 21 SCL
  Comunicatie LCD Display I2C

custom parts:
  L298N DC motor driver: 2x DC motor driver with 78M05 positive voltage regulator (7..35 V) L298N: max 46 V, 2 A Set 5 V Enable jumper to enable 5 V regultor (needed for the L298N) and +5 V output at screw terminal or supply external +5 V at screw terminal Set ENA and/or ENB to +5 V to enable motor permanently or supply ENA and/or ENB with PWM signal IN1 and IN2 set rotation directory for motor A (OUT1/OUT2) IN2 and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
  TCRT5000: TCRT5000 optical reflective sensor
  D2F-FL Omron Snap Action Limit Switch with Level: Snap action switch with stainless steel lever.
  LCD2004-I2C: A standard character display with 4x20 characters. Comes in many colors with LCM2004 IIC attached.
  WS2812 RGB LED matrix 1x8: WS2812 matrix 1x8
